# Fritzing sketch ckt balanca IoT (saved by Fritzing 0.9.3b)
breadboards: 1

parts:
  J1 = Basic Force Sensing Resistor (FSR) [package=THT]
  U1 = NodeMCU V1.0  # not connected
  R1 = Resistor [tolerance=±5% resistance=1k package="0603 [SMD]"]
  S2 = Round Pushbutton

nets:
  N1: J1.pin_1, R1.Pin_0
  N2: R1.Pin_1, S2.leg1

custom parts:
  NodeMCU V1.0: ESP8266 based NodeMCU
